# Fritzing sketch ButtonPcb (saved by Fritzing 0.9.3b)
circuit board: 9.12531cm x 3.01667cm
breadboards: 1

parts:
  S1 = SWITCH-MOMENTARY-2 [package=tactile-pth-12mm]
  S2 = SWITCH-MOMENTARY-2 [package=tactile-pth-12mm]
  S3 = SWITCH-MOMENTARY-2 [package=tactile-pth-12mm]
  S4 = SWITCH-MOMENTARY-2 [package=tactile-pth-12mm]
  S5 = SWITCH-MOMENTARY-2 [package=tactile-pth-12mm]
  R1 = Resistor [tolerance=±5% resistance=1k package=THT]
  R2 = Resistor [tolerance=±5% resistance=1k package=THT]
  R3 = Resistor [tolerance=±5% resistance=1k package=THT]
  R4 = Resistor [tolerance=±5% resistance=1k package=THT]
  R5 = Resistor [tolerance=±5% resistance=2.2k package=THT]
  J1 = male pin header, 3 pins [form="♂ (male)"]

nets:
  N1: S1.1, R1.Pin_0, R5.Pin_1, J1.pin2
  GND: S1.2, S2.2, S3.2, S4.2, S5.2, J1.pin3
  N2: S2.1, R1.Pin_1, R2.Pin_0
  N3: S3.1, R2.Pin_1, R3.Pin_0
  N4: S4.1, R3.Pin_1, R4.Pin_0
  N5: S5.1, R4.Pin_1
  N6: R5.Pin_0, J1.pin1
